# Fritzing sketch Ma-I-am-homefzz (saved by Fritzing 0.9.3b)
breadboards: 1

parts:
  Gizwits_WiFi_Witty_ESP-12F1 = Gizwits WiFi Witty ESP-12F
  LED1 = smd LED [color="Red (633nm)" package="0603 [SMD]"]
  R1 = Resistor [tolerance=±5% resistance=220 package="0805 [SMD]"]
  S1 = Momentary Switch [package=ksa_sealed_tac_switch]
  VCC1 = Battery
  Part1 = FTDI Basic Programmer

nets:
  N1: Gizwits_WiFi_Witty_ESP-12F1.REST, S1.3
  N2: Gizwits_WiFi_Witty_ESP-12F1.CH_PD, Gizwits_WiFi_Witty_ESP-12F1.VCC, R1.Pin_1, VCC1.+
  GND: Gizwits_WiFi_Witty_ESP-12F1.GND, S1.1, VCC1.-, Part1.GND
  N3: Gizwits_WiFi_Witty_ESP-12F1.GPIO0, Part1.DTR
  N4: Gizwits_WiFi_Witty_ESP-12F1.GPIO5, LED1.cathode
  N5: Gizwits_WiFi_Witty_ESP-12F1.RXD, Part1.TXO
  N6: Gizwits_WiFi_Witty_ESP-12F1.TXD, Part1.RXI
  N7: LED1.anode, R1.Pin_0

notes:
  My FTDI has a RTS header connected to RESET
